# Fritzing sketch thermostat (saved by Fritzing 0.9.6b)
breadboards: 1

parts:
  MCU1 = Raspberry Pi Zero
  Part2 = Barometric Pressure Sensor - BMP180 Breakout (GY-68)
  RE1 = KY-040 Rotary encoder [package=THT]
  LCD4 = TFT 1.8 inch 160x128 no SD
  LED1 = LED - 5mm [color="Red (633nm)" current=0.030 package="5 mm [THT]"]
  R1 = Resistor [tolerance=±5% resistance=220 package="1206 [SMD]"]

nets:
  VCC: MCU1.pin_1, MCU1.pin_17, Part2.VCC, RE1.Vcc, LCD4.pin_8
  N1: MCU1.pin_3, Part2.SDA
  N2: MCU1.pin_5, Part2.SCL
  GND: MCU1.pin_6, MCU1.pin_9, MCU1.pin_34, MCU1.pin_39, Part2.GND, RE1.GND, LCD4.pin2, LED1.anode
  N3: MCU1.pin_7, MCU1.pin_8, R1.Pin_0
  N4: MCU1.pin_12, LCD4.pin_7
  N5: MCU1.pin_18, LCD4.pin4
  N6: MCU1.pin_22, LCD4.pin3
  N7: MCU1.pin_29, RE1.CLK
  N8: MCU1.pin_31, RE1.DT
  N9: MCU1.pin_37, RE1.SW
  N10: MCU1.pin_38, LCD4.pin_5
  N11: MCU1.pin_40, LCD4.pin_6
  N12: LED1.cathode, R1.Pin_1

custom parts:
  KY-040 Rotary encoder: KY-040 Rotary Encoder with switch on breakout borad from AZ Delivery
  TFT 1.8 inch 160x128 no SD: This is a generic 1.8 tft spi lcd display available on ebay and others. The 1.8" display has 128x160 color pixels and in this version pin names in breadboard (unlike the real board) and with no SD interface.
